# Fritzing sketch rfid_doorlock_fritzing (saved by Fritzing 0.6.3b)
breadboards: 1

parts:
  Arduino1 = Arduino Mega
  R1 = Resistor [tolerance=±5% resistance=470 package=THT]
  U1 = Optocoupler [part_number=4N35 package=THT]
  RFID1 = RFID Reader
  Power_plug1 = Power plug
  L1 = Solenoid
  Q1 = npn-Powertransistor [package="TO220 [THT]"]
  LED1 = LED - 5mm [color="Red (633nm)" package="5 mm [THT]"]
  LED2 = LED - 5mm [color="Green (560nm)" package="5 mm [THT]"]
  R2 = Resistor [tolerance=±5% resistance=470 package=THT]
  R3 = Resistor [tolerance=±5% resistance=470 package=THT]

nets:
  N1: Arduino1.D2, R1.Pin_0
  +5V: Arduino1.+5V, RFID1.+5V
  GND: Arduino1.GND, U1.Pin_2, RFID1.GND
  N2: Arduino1.A2, RFID1.+/-
  N3: Arduino1.D20, RFID1.D0
  N4: Arduino1.D21, RFID1.D1
  N5: R1.Pin_1, LED1.cathode
  N6: U1.Pin_1, LED1.anode
  N7: U1.Pin_4, Q1.base
  N8: U1.Pin_5, Power_plug1.VCC, L1.pin2, R3.Pin_1
  N9: Power_plug1.GND, Q1.emitter
  N10: L1.pin1, Q1.collector, LED2.cathode
  N11: R2.Pin_0, R3.Pin_0
